# Fritzing sketch pico_pedometer_circuit (saved by Fritzing 0.9.10b)
breadboards: 1

parts:
  Part1 = Adafruit LSM9DS1 9DoF Breakout [part_number="Adafruit #3387"]
  Mod1 = Raspberry Pi Pico
  IC1 = Voltage Regulator [package=to-220-alt]
  VCC1 = Battery block 9V

nets:
  N1: Part1.SDA, Mod1.pin_24
  N2: Part1.SCL, Mod1.pin_25
  N3: Part1.GND, Mod1.pin_3, Mod1.pin_8, Mod1.pin_13, Mod1.pin_18, Mod1.pin_23, Mod1.pin_28, Mod1.pin_33, Mod1.pin_38, Mod1.pin_42, IC1.IN, VCC1.-
  N4: Part1.VIN, Mod1.pin_36
  N5: Mod1.pin_39, IC1.OUT
  N6: IC1.GND, VCC1.+

custom parts:
  Adafruit LSM9DS1 9DoF Breakout: Add motion, direction and orientation sensing to your Arduino project with this all-in-one 9-DOF sensor. Inside the chip are three sensors, one is a classic 3-axis accelerometer, which can tell you which direction is down towards the Earth (by measuring gravity) or how fast the board is accelerating in 3D space. The other is a 3-axis magnetometer that can sense where the strongest magnetic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
  Raspberry Pi Pico: Raspberry Pi Pico. Based around the RP2040 microcontroller the Pico is a low cost microcontroller device bringing Raspberry Pi quality, cost, and easy of use to the microcontroller space. Jan 2021, Split part in to two versions: tht (this one) and SMD. This one will drill holes for a .1 in header in pcb to allow plugging in the module as well as providing pads to solder the module to the top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
